# Fritzing sketch LED_INFRAROSSI (saved by Fritzing 0.6.3b)
breadboards: 1

parts:
  Arduino1 = Arduino
  LED1 = LED - 5mm [color="Infrared (940nm)" package="5 mm [THT]"]
  LED2 = LED - 5mm [color="Infrared (940nm)" package="5 mm [THT]"]

nets:
  N1: Arduino1.A0, LED1.anode
  N2: Arduino1.A1, LED2.anode
  N3: LED1.cathode, LED2.cathode
