# Fritzing sketch LED_RGB (saved by Fritzing 0.6.3b)
breadboards: 1

parts:
  Arduino1 = Arduino
  R1 = Resistor [tolerance=±5% resistance=330 package=THT]
  R2 = Resistor [tolerance=±5% resistance=330 package=THT]
  R3 = Resistor [tolerance=±5% resistance=330 package=THT]
  LED1 = RGB LED (com. cathode, rbg) [package="5 mm [THT]"]
  S1 = Pushbutton [package="[THT]"]
  S2 = Pushbutton [package="[THT]"]
  S3 = Pushbutton [package="[THT]"]
  R4 = Resistor [tolerance=±5% resistance=330 package=THT]
  R5 = Resistor [tolerance=±5% resistance=330 package=THT]
  R6 = Resistor [tolerance=±5% resistance=330 package=THT]

nets:
  N1: Arduino1.D13, R1.Pin_1
  N2: Arduino1.D12, R2.Pin_1
  N3: Arduino1.D11, R3.Pin_1
  N4: Arduino1.D7, S1.Pin_1, S1.Pin_2, R4.Pin_1
  N5: Arduino1.D6, S2.Pin_1, S2.Pin_2, R5.Pin_1
  N6: Arduino1.D5, S3.Pin_1, S3.Pin_2, R6.Pin_1
  N7: Arduino1.+5V, S1.Pin_3, S1.Pin_4, S2.Pin_3, S2.Pin_4, S3.Pin_3, S3.Pin_4
  N8: Arduino1.GND, R4.Pin_0, R5.Pin_0, R6.Pin_0
  N9: R1.Pin_0, LED1.red_anode
  N10: R2.Pin_0, LED1.blue_anode
  N11: R3.Pin_0, LED1.green_anode
