# Fritzing sketch semaforo (saved by Fritzing 0.6.3b)
breadboards: 1

parts:
  Arduino1 = Arduino
  LED1 = LED - 5mm [color="Red (633nm)" package="5 mm [THT]"]
  LED3 = LED - 5mm [color="Green (560nm)" package="5 mm [THT]"]
  LED2 = smd LED [color="Yellow (595nm)" package="0603 [SMD]"]
  R1 = Resistor [tolerance=±5% resistance=330 package=THT]
  R2 = Resistor [tolerance=±5% resistance=330 package=THT]
  R3 = Resistor [tolerance=±5% resistance=330 package=THT]

nets:
  N1: Arduino1.GND, R1.Pin_1, R3.Pin_1
  N2: Arduino1.D13, LED1.anode
  N3: Arduino1.D12, LED2.anode
  N4: Arduino1.D11, LED3.anode
  N5: LED1.cathode, R1.Pin_0
  N6: LED3.cathode, R3.Pin_0
  N7: LED2.cathode, R2.Pin_0
