# Fritzing sketch Untitled Sketch (saved by Fritzing 0.6.3b)
breadboards: 1

parts:
  Arduino1 = Arduino
  R1 = Photocell (LDR) [package=THT]
  R2 = Resistor [tolerance=±5% resistance=1k package=THT]
  LED1 = LED - 5mm [color="Red (633nm)" package="5 mm [THT]"]
  R3 = Resistor [tolerance=±5% resistance=330 package=THT]

nets:
  N1: Arduino1.D13, LED1.anode
  N2: Arduino1.GND, R1.pin_0
  N3: Arduino1.A0, R1.pin_1, R2.Pin_0
  N4: LED1.cathode, R3.Pin_1
